# Fritzing sketch Sprint1 (saved by Fritzing 0.9.3b)
breadboards: 1

parts:
  Pololu_A1 = Pololu A4988 [package=SO16]
  Pololu_A2 = Pololu A4988 [package=SO16]
  Part1 = Arduino Uno (Rev3)
  M1 = Stepper Motor - Bipolar
  M2 = Stepper Motor - Bipolar
  V1 = DC Power [voltage=12V]

nets:
  VDD: Pololu_A1.ENABLE, Pololu_A1.VDD, Pololu_A2.VDD, Part1.5V
  N1: Pololu_A1.MS1, Pololu_A2.MS1, Part1.D10_PWM/SS
  N2: Pololu_A1.MS2, Pololu_A2.MS2, Part1.D11_PWM/MOSI
  N3: Pololu_A1.MS3, Pololu_A2.MS3, Part1.D12/MISO
  N4: Pololu_A1.RESET, Pololu_A1.SLEEP
  N5: Pololu_A1.STEP, Part1.D4
  N6: Pololu_A1.DIR, Part1.D3_PWM
  N7: Pololu_A1.1B, M1.D
  N8: Pololu_A1.1A, M1.B
  N9: Pololu_A1.2A, M1.C
  N10: Pololu_A1.2B, M1.A
  N11: Pololu_A1.VMOT, Pololu_A2.VMOT, V1.V+
  N12: Pololu_A2.RESET, Pololu_A2.SLEEP
  N13: Pololu_A2.STEP, Part1.D9_PWM
  N14: Pololu_A2.DIR, Part1.D8
  GND: Pololu_A2.GND, Part1.GND, V1.V-
  N15: Pololu_A2.1B, M2.D
  N16: Pololu_A2.1A, M2.B
  N17: Pololu_A2.2A, M2.C
  N18: Pololu_A2.2B, M2.A
